// Logisim project testing.circ as structural Verilog: 2 circuits, main circuit main
module main (
  input  [7:0] in_1,
  input  in_2,
  input  in_3,
  output [7:0] out_4,
  output out_5,
  output out_6,
  output out_7,
  output out_8,
  output out_9
);

  wire clock_1_out, shift_register_1_out;

  Clock clock_1 (.out(clock_1_out));
  Register register_1 (.D(in_1), .en(in_2), .Q(out_4), .clk(clock_1_out));  // open: clr
  Shift_Register shift_register_1 (
    .shift(in_2), .in(in_3), .clk(clock_1_out), .out(shift_register_1_out), .q0(out_6), .q5(out_7),
    .q6(out_8), .q7(out_9));  // open: load, clr, d0, d1, q1, d2, q2, d3, q3, d4, q4, d5, d6, d7
  Shifter shifter_1 ();  // open: in, dist, out
endmodule

module restoring (
  input  [7:0] D,
  input  [15:0] UV,
  output [15:0] out_3,
  output [2:0] out_4,
  output [7:0] out_5,
  output [7:0] out_6
);

  wire button_1_out, clock_1_out, comparator_1_gt;

  Button button_1 (.out(button_1_out));
  Clock clock_1 (.out(clock_1_out));
  Counter #(.width(3), .max('h7), .ongoal("stay")) counter_1 (
    .Q(out_4), .clk(clock_1_out), .clr(button_1_out));  // open: load, D, count, carry
  Shifter #(.width(16)) shifter_1 (.in(UV), .\dist (4'b0001), .out(out_3));
  Comparator #(.mode("unsigned")) comparator_1 (.a(out_3[15:8]), .b(D), .gt(comparator_1_gt));  // open: eq, lt

  assign out_5 = out_3[7:0];
  assign out_6 = out_3[15:8];
endmodule
