// Logisim project try1.circ as structural Verilog: 1 circuit, main circuit main
module main (
  input  in_1,
  input  in_2,
  input  [1:0] in_3,
  input  [1:0] in_4,
  input  in_5,
  output out_6,
  output out_7,
  output out_8
);

  wire adder_1_out, and_1_out, and_2_out, and_3_out, not_1_out, not_2_out, not_3_out, or_1_out;

  not not_1 (not_1_out, in_1);
  not not_2 (not_2_out, in_2);
  and and_1 (and_1_out, not_1_out, in_2);
  and and_2 (and_2_out, in_1, not_2_out);
  not not_3 (not_3_out, in_3[0]);
  Adder #(.width(1)) adder_1 (.a(in_3[0]), .b(in_3[1]), .out(adder_1_out), .cin(in_5), .cout(out_8));
  and and_3 (and_3_out, in_3[0], in_3[1]);
  or or_1 (or_1_out, in_3[0], in_3[1]);
  or or_2 (out_6, and_1_out, and_2_out);
  Multiplexer #(.select(2), .enable("false")) multiplexer_1 (
    .in0(and_3_out), .in1(or_1_out), .in2(not_3_out), .in3(adder_1_out), .out(out_7), .sel(in_4));
endmodule
